// Logisim project main.circ as structural Verilog: 5 circuits, main circuit main
module main (
);

  wire check_collision, clock_1_out, collision, decoder_1_pixel_state__bit_8, decoder_1_write__bit_9,
       game_over;
  wire [3:0] decoder_1_x_coord__bits_0_3, decoder_1_y_coord__bits_4_7, keyboard;
  wire [6:0] keyboard_1_data;
  wire [15:0] display, display_controller_1_c00, display_controller_1_c01, display_controller_1_c02,
       display_controller_1_c03, display_controller_1_c04, display_controller_1_c05,
       display_controller_1_c06, display_controller_1_c07, display_controller_1_c08,
       display_controller_1_c09, display_controller_1_c10, display_controller_1_c11,
       display_controller_1_c12, display_controller_1_c13, display_controller_1_c14, display_controller_1_c15;

  // Debugger debugger_1: pin names not known
  computer computer_1 (
    .keyboard(keyboard), .check_collision(check_collision), .game_over(game_over), .display(display),
    .collision(collision));
  decoder decoder_1 (
    .in_1(display), .X_coord__bits_0_3(decoder_1_x_coord__bits_0_3),
    .Y_coord__bits_4_7(decoder_1_y_coord__bits_4_7), .pixel_state__bit_8(decoder_1_pixel_state__bit_8),
    .write__bit_9(decoder_1_write__bit_9));
  DotMatrix #(.matrixcols(16), .matrixrows(16)) dotmatrix_1 (
    .col0(display_controller_1_c00), .col1(display_controller_1_c01), .col2(display_controller_1_c02),
    .col3(display_controller_1_c03), .col4(display_controller_1_c04), .col5(display_controller_1_c05),
    .col6(display_controller_1_c06), .col7(display_controller_1_c07), .col8(display_controller_1_c08),
    .col9(display_controller_1_c09), .col10(display_controller_1_c10), .col11(display_controller_1_c11),
    .col12(display_controller_1_c12), .col13(display_controller_1_c13), .col14(display_controller_1_c14),
    .col15(display_controller_1_c15));
  display_controller display_controller_1 (
    .X_coord(decoder_1_x_coord__bits_0_3), .Y_coord(decoder_1_y_coord__bits_4_7),
    .pixel_state(decoder_1_pixel_state__bit_8), .write(decoder_1_write__bit_9),
    .c00(display_controller_1_c00), .pixel_check(check_collision), .c01(display_controller_1_c01),
    .c02(display_controller_1_c02), .c03(display_controller_1_c03), .c04(display_controller_1_c04),
    .c05(display_controller_1_c05), .c06(display_controller_1_c06), .c07(display_controller_1_c07),
    .c08(display_controller_1_c08), .c09(display_controller_1_c09), .c10(display_controller_1_c10),
    .c11(display_controller_1_c11), .c12(display_controller_1_c12), .c13(display_controller_1_c13),
    .c14(display_controller_1_c14), .c15(display_controller_1_c15), .checked(collision), .game_over(game_over));
  Keyboard keyboard_1 (.clk(clock_1_out), .data(keyboard_1_data));  // open: re, clr, avail
  Clock clock_1 (.out(clock_1_out));
  keyboard_decoder keyboard_decoder_1 (.keyboard_input(keyboard_1_data), .keyboard_output(keyboard));

  // Notes on the sheet:
  //   Тут мы ставим кнопки для управления змеёй
  //   Тут мы ставим счётчик
endmodule

module memory_map_extrude (
  input  [15:0] addr,
  input  [15:0] constant,
  input  store_start_address,
  output [3:0] out_4,
  output map_active
);

  wire and_1_out, and_2_out, and_4_out, and_5_out, and_6_out, clock_1_out, multiplexer_2_out,
       multiplexer_3_out, not_1_out, not_2_out, not_3_out, not_4_out, not_5_out, not_6_out, not_7_out,
       not_8_out, not_9_out, not_10_out, not_11_out, pull_resistor_1_node, t_ff_1_q, t_ff_1_qn, undriven;
  wire [11:0] xnor_1_out;
  wire [15:0] multiplexer_1_out, register_1_q;
  wire [15:4] subtractor_1_out;

  not not_1 (not_1_out, not_2_out);
  not not_2 (not_2_out, undriven);
  Pull_Resistor pull_resistor_1 (.node(pull_resistor_1_node));
  not not_3 (not_3_out, undriven);
  assign pull_resistor_1_node = not_3_out ? 1'b1 : 1'bz;  // Controlled_Buffer controlled_buffer_1
  Multiplexer #(.width(16)) multiplexer_1 (
    .in0(constant), .in1(16'h8000), .out(multiplexer_1_out), .sel(not_4_out));  // open: en
  not not_4 (not_4_out, not_5_out);
  not not_5 (not_5_out, not_6_out);
  not not_6 (not_6_out, not_7_out);
  not not_7 (not_7_out, not_8_out);
  not not_8 (not_8_out, store_start_address);
  not not_9 (not_9_out, not_10_out);
  not not_10 (not_10_out, not_1_out);
  assign pull_resistor_1_node = not_9_out ? 1'b1 : 1'bz;  // Controlled_Buffer controlled_buffer_2
  Register #(.width(16)) register_1 (.D(multiplexer_1_out), .Q(register_1_q), .clk(and_1_out));  // open: en, clr
  and and_1 (and_1_out, not_8_out, multiplexer_2_out);
  Multiplexer multiplexer_2 (
    .in0(store_start_address), .in1(multiplexer_3_out), .out(multiplexer_2_out), .sel(not_8_out));  // open: en
  Subtractor #(.width(16)) subtractor_1 (
    .a(addr), .b(register_1_q), .out({subtractor_1_out, out_4}));  // open: bin, bout
  Multiplexer multiplexer_3 (.in0(not_11_out), .in1(1'b0), .out(multiplexer_3_out), .sel(t_ff_1_q));  // open: en
  T_Flip_Flop t_ff_1 (
    .clk(store_start_address), .T(t_ff_1_qn), .Q(t_ff_1_q), .Qn(t_ff_1_qn));  // open: preset, reset, en
  not not_11 (not_11_out, clock_1_out);
  Clock clock_1 (.out(clock_1_out));
  assign xnor_1_out = ~(subtractor_1_out ^ {12{1'b0}});  // XNOR_Gate xnor_1, 12 bits wide
  and and_2 (and_2_out, xnor_1_out[11], xnor_1_out[10], xnor_1_out[9]);
  and and_3 (map_active, and_2_out, and_5_out, and_4_out, and_6_out);
  and and_4 (and_4_out, xnor_1_out[5], xnor_1_out[4], xnor_1_out[3]);
  and and_5 (and_5_out, xnor_1_out[8], xnor_1_out[7], xnor_1_out[6]);
  and and_6 (and_6_out, xnor_1_out[2], xnor_1_out[1], xnor_1_out[0]);
endmodule

module random_generator (
  input  get_random,
  output [15:0] random_XY
);

  wire [7:0] random_1_out;

  Random #(.trigger("falling")) random_1 (.clk(get_random), .out(random_1_out));  // open: next, clr
  assign random_XY = {{8{1'b0}}, random_1_out};  // Bit_Extender bit_extender_1
endmodule

module keyboard_decoder (
  input  [6:0] keyboard_input,
  output [3:0] keyboard_output
);

  wire and_1_out, clock_1_out, or_1_out;
  wire [3:0] not_1_out, not_2_out, out;

  assign not_1_out = ~out;  // NOT_Gate not_1, 4 bits wide
  assign not_2_out = ~not_1_out;  // NOT_Gate not_2, 4 bits wide
  or or_1 (or_1_out, out[0], out[1], out[3], out[2]);
  Comparator #(.width(7)) comparator_1 (.a(keyboard_input), .b(7'b1110111), .eq(out[0]));  // open: gt, lt
  Comparator #(.width(7)) comparator_2 (.a(keyboard_input), .b(7'b1100100), .eq(out[1]));  // open: gt, lt
  Comparator #(.width(7)) comparator_3 (.a(keyboard_input), .b(7'b1110011), .eq(out[2]));  // open: gt, lt
  Comparator #(.width(7)) comparator_4 (.a(keyboard_input), .b(7'b1100001), .eq(out[3]));  // open: gt, lt
  Register #(.width(4)) register_1 (.D(not_2_out), .Q(keyboard_output), .clk(and_1_out));  // open: en, clr
  and and_1 (and_1_out, or_1_out, clock_1_out);
  Clock clock_1 (.out(clock_1_out));
endmodule

module computer (
  input  collision,
  input  [3:0] keyboard,
  output [15:0] display,
  output check_collision,
  output game_over
);

  wire and_1_out, and_2_out, cdm_16_1_p2, clock_2_out, clock_3_out, mem_sel, memory,
       memory_map_extrude_1_map_active, not_1_out, read_write, store_start_address, word;
  wire [3:0] memory_map_extrude_1_out_4;
  wire [15:0] address, cdm_16_1_p4, cdm_16_1_p9, cdm_16_1_p10, data, multiplexer_1_out, s00, s01, s02, s03,
       s04, s05, s06, s07, s08, s09, s10, s11, s12, s13, s14, s15, start_address;

  // Probe on display
  // CdM_16 cdm_16_1: pin names not known; wires that end beside it: display, cdm_16_1_p2, start_address, {cdm_16_1_p4[15:4], store_start_address, game_over, check_collision, cdm_16_1_p4[0]}, memory, read_write, word, address, cdm_16_1_p9, cdm_16_1_p10
  Clock clock_1 (.out(cdm_16_1_p2));
  random_generator random_generator_1 (.get_random(cdm_16_1_p4[0]), .random_XY(s01));
  assign data = not_1_out ? cdm_16_1_p9 : 16'bz;  // Controlled_Buffer controlled_buffer_1
  not not_1 (not_1_out, read_write);
  assign cdm_16_1_p10 = read_write ? data : 16'bz;  // Controlled_Buffer controlled_buffer_2
  Clock clock_2 (.out(clock_2_out));
  memory_map_extrude memory_map_extrude_1 (
    .addr(address), .constant(start_address), .out_4(memory_map_extrude_1_out_4),
    .map_active(memory_map_extrude_1_map_active), .store_start_address(store_start_address));
  and and_1 (and_1_out, memory, mem_sel);
  Clock clock_3 (.out(clock_3_out));
  assign data = and_2_out ? multiplexer_1_out : 16'bz;  // Controlled_Buffer controlled_buffer_3
  not not_2 (mem_sel, and_2_out);
  and and_2 (and_2_out, read_write, clock_2_out, memory_map_extrude_1_map_active);
  // RAM ram_1: pin names not known; wires that end beside it: address, word, and_1_out, clock_3_out, read_write, data
  Multiplexer #(.select(4), .width(16)) multiplexer_1 (
    .in0(s00), .in1(s01), .in2(s02), .in3(s03), .in4(s04), .in5(s05), .in6(s06), .in7(s07), .in8(s08),
    .in9(s09), .in10(s10), .in11(s11), .in12(s12), .in13(s13), .in14(s14), .in15(s15),
    .out(multiplexer_1_out), .sel(memory_map_extrude_1_out_4), .en(1'b1));
  assign s02 = {{15{1'b0}}, collision};  // Bit_Extender bit_extender_1
  assign s00 = {{12{1'b0}}, keyboard};  // Bit_Extender bit_extender_2
endmodule
